# Fritzing sketch TB6612FNG_motor_control (saved by Fritzing 0.9.3b)
breadboards: 1

parts:
  Composant1 = Arduino Uno (Rev3)
  PART2 = Motor Driver 1A Dual TB6612FNG [part_number=ROB_09457]
  M1 = DC Motor
  Power_plug1 = Power plug
  M2 = DC Motor

nets:
  N1: Composant1.D8, PART2.AIN2
  N2: Composant1.D9_PWM, PART2.AIN1
  N3: Composant1.D10_PWM/SS, PART2.STBY
  N4: Composant1.D11_PWM/MOSI, PART2.BIN1
  N5: Composant1.D12/MISO, PART2.BIN2
  GND: Composant1.GND, PART2.GND, Power_plug1.GND
  N6: Composant1.D3_PWM, PART2.PWMB
  N7: Composant1.D5_PWM, PART2.PWMA
  5V: Composant1.5V, PART2.VCC
  N8: PART2.VM, Power_plug1.VCC
  N9: PART2.A01, M1.pin_1
  N10: PART2.A02, M1.pin_2
  N11: PART2.B02, M2.pin_2

custom parts:
  Motor Driver 1A Dual TB6612FNG: The TB6612FNG motor driver can control up to two DC motors at a constant current of 1.2A (3.2A peak). Two input signals (IN1 and IN2) can be used to control the motor in one of four function modes - CW, CCW, short-brake, and stop. The two motor outputs (A and B) can be separately controlled, the speed of each motor is controlled via a PWM input signal with a frequency up to 100kHz. The STBY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

// code stored in the sketch: TB6612FNG_motor_control.ino
//motor A connected between A01 and A02
//motor B connected between B01 and B02

int STBY = 10; //standby

//Motor A
int PWMA = 5; //Speed control
int AIN1 = 9; //Direction
int AIN2 = 8; //Direction

//Motor B
int PWMB = 3; //Speed control
int BIN1 = 11; //Direction
int BIN2 = 12; //Direction

void setup(){
pinMode(STBY, OUTPUT);

pinMode(PWMA, OUTPUT);
pinMode(AIN1, OUTPUT);
pinMode(AIN2, OUTPUT);

pinMode(PWMB, OUTPUT);
pinMode(BIN1, OUTPUT);
pinMode(BIN2, OUTPUT);
}

void loop(){
move(1, 200, 1); //motor 1, full speed, left
move(2, 200, 1); //motor 2, full speed, left

delay(1000); //go for 1 second
stop(); //stop
delay(250); //hold for 250ms until move again

move(1, 128, 0); //motor 1, half speed, right
move(2, 128, 0); //motor 2, half speed, right

delay(1000);
stop();
delay(250);
}

void move(int motor, int speed, int direction){
//Move specific motor at speed and direction
//motor: 0 for B 1 for A
//speed: 0 is off, and 255 is full speed
//direction: 0 clockwise, 1 counter-clockwise

digitalWrite(STBY, HIGH); //disable standby

boolean inPin1 = LOW;
boolean inPin2 = HIGH;

if(direction == 1){
inPin1 = HIGH;
inPin2 = LOW;
}

if(motor == 1){
digitalWrite(AIN1, inPin1);
digitalWrite(AIN2, inPin2);
analogWrite(PWMA, speed);
}else{
digitalWrite(BIN1, inPin1);
digitalWrite(BIN2, inPin2);
analogWrite(PWMB, speed);
}
}

void stop(){
//enable standby
digitalWrite(STBY, LOW);
}
