# Fritzing sketch detecteur_intrusion_HC-SR04 (saved by Fritzing 0.9.3b)
breadboards: 1

parts:
  Composant1 = Arduino Uno (Rev3)
  R1 = Resistor [tolerance=±5% resistance=220 package=THT]
  LED1 = LED - 5mm [color="Red (633nm)" package="5 mm [THT]"]
  hc-sr1 = hc-sr04
  MIC1 = Microphone

nets:
  N1: Composant1.D8, MIC1.pin2
  N2: Composant1.D12/MISO, R1.Pin_1
  GND: Composant1.GND, LED1.cathode, hc-sr1.GND, MIC1.pin1
  N3: Composant1.D2, hc-sr1.Trig
  N4: Composant1.D3_PWM, hc-sr1.Echo
  5V: Composant1.5V, hc-sr1.VCC
  N5: R1.Pin_0, LED1.anode

// code stored in the sketch: detecteur_intrusion_HC-SR04.ino
/* 
 * Code d'exemple pour un capteur à ultrasons HC-SR04.
 */

/* Constantes pour les broches */
const byte TRIGGER_PIN = 2; // Broche TRIGGER
const byte ECHO_PIN = 3;    // Broche ECHO
const byte LED_PIN = 12;  // Broche LED
const byte PIEZO_PIN = 8;  // Broche PIEZO

 
/* Constantes pour le timeout */
const unsigned long MEASURE_TIMEOUT = 50000UL; // 25ms = ~8m à 340m/s

/* Vitesse du son dans l'air en mm/us */
const float SOUND_SPEED = 340.0 / 1000;

/** Fonction setup() */
void setup() {
   
  /* Initialise le port série */
  Serial.begin(115200);
   
  /* Initialise les broches */
  pinMode(TRIGGER_PIN, OUTPUT);
  digitalWrite(TRIGGER_PIN, LOW); // La broche TRIGGER doit être à LOW au repos
 
  pinMode(LED_PIN, OUTPUT);
  digitalWrite(LED_PIN, LOW);

  pinMode(ECHO_PIN, INPUT);
}
 
/** Fonction loop() */
void loop() {
  
  /* 1. Lance une mesure de distance en envoyant une impulsion HIGH de 10µs sur la broche TRIGGER */
  digitalWrite(TRIGGER_PIN, HIGH);
  delayMicroseconds(10);
  digitalWrite(TRIGGER_PIN, LOW);
  
  /* 2. Mesure le temps entre l'envoi de l'impulsion ultrasonique et son écho (si il existe) */
  long measure = pulseIn(ECHO_PIN, HIGH, MEASURE_TIMEOUT);
   
  /* 3. Calcul la distance à partir du temps mesuré */
  float distance_mm = measure / 2.0 * SOUND_SPEED;

  if(distance_mm/1000 < 1){
    digitalWrite(LED_PIN, HIGH);
    tone(PIEZO_PIN, 294);
  }
  
  /* Affiche les résultats en mm, cm et m 
  Serial.print(F("Distance: "));
  Serial.print(distance_mm / 1000.0, 2);
  Serial.println(F("m)"));
   */

  /* Délai d'attente pour éviter d'afficher trop de résultats à la seconde */
  delay(200);
  
  digitalWrite(LED_PIN, LOW);
  noTone(PIEZO_PIN);

}
